# Fritzing sketch Smart Pump Controller-v1.1 (saved by Fritzing 0.9.2b)
circuit board: 7.62cm x 7.62cm
breadboards: 1

parts:
  9V_DC = Deb Screw terminal - 2 pins, spacing 0.2in (5.08mm) [package=THT]
  5V = female pin header, 2 pins [form="♀ (female)"]
  5V_2 = female pin header, 2 pins [form="♀ (female)"]
  5V_3 = female pin header, 2 pins [form="♀ (female)"]
  3_3V = female pin header, 2 pins [form="♀ (female)"]
  3_3V_2 = female pin header, 2 pins [form="♀ (female)"]
  D1 = Rectifier Diode [part_number=1N4007 package="300 mil [THT]"]
  HS1 = Deb TO-220 Normal Heat Sink  # not connected
  HS2 = Deb TO-220 Normal Heat Sink  # not connected
  VR1 = Voltage Regulator [package=78xxl]
  VR2 = Voltage Regulator [package=78xxl]
  On/Off = Deb Screw terminal - 2 pins, spacing 0.2in (5.08mm) [package=THT]
  LED1 = LED - 5mm [color="Red (633nm)" package="5 mm [THT]"]
  R1 = Resistor [tolerance=±5% resistance=560 package=THT]
  C1 = Electrolytic Capacitor [capacitance=100µF voltage=20V package="100 mil [THT, electrolytic]"]
  C2 = Electrolytic Capacitor [capacitance=100µF voltage=20V package="100 mil [THT, electrolytic]"]
  C3 = Electrolytic Capacitor [capacitance=10µF voltage=20V package="100 mil [THT, electrolytic]"]
  C4 = Electrolytic Capacitor [capacitance=10µF voltage=20V package="100 mil [THT, electrolytic]"]
  MC = Digispark
  Relay = female pin header, 3 pins [form="♀ (female)"]
  R2 = Resistor [tolerance=±5% resistance=330 package=THT]
  LED2 = LED - 5mm [color="Red (633nm)" package="5 mm [THT]"]
  VR3 = V_REG_LD1117VXX [package=78xxl]
  C5 = Electrolytic Capacitor [capacitance=10µF voltage=20V package="100 mil [THT, electrolytic]"]
  TSOP = female pin header, 4 pins [form="♀ (female)"]
  C6 = Electrolytic Capacitor [capacitance=10µF voltage=20V package="100 mil [THT, electrolytic]"]
  C7 = Ceramic Capacitor [capacitance=100nF voltage=20V package="200 mil [THT, multilayer]"]
  R3 = Resistor [tolerance=±5% resistance=100 package=THT]
  LED3 = LED - 5mm [color="Red (633nm)" package="5 mm [THT]"]
  ext_pin = female pin header, 3 pins [form="♀ (female)"]
  Push_S/W = Deb Screw terminal - 2 pins, spacing 0.2in (5.08mm) [package=THT]
  R4 = Resistor [tolerance=±5% resistance=10k package=THT]
  5V_4 = female pin header, 2 pins [form="♀ (female)"]
  JP = female pin header, 3 pins [form="♀ (female)"]

nets:
  N1: 9V_DC.pin1, D1.anode
  GND: 9V_DC.pin2, 5V.pin1, 5V_2.pin1, 5V_3.pin1, 3_3V.pin1, 3_3V_2.pin1, VR1.GND, VR2.GND, LED1.cathode, C1.-, C2.-, C3.-, C4.-, MC.GND, Relay.pin1, VR3.GND, C5.-, TSOP.pin1, C6.-, C7.1, R4.Pin_0, 5V_4.pin1
  N2: 5V.pin2, VR1.OUT, C3.+, VR3.IN, C7.0, Push_S/W.pin1, 5V_4.pin2, JP.pin2
  N3: 5V_2.pin2, 5V_3.pin2, VR2.OUT, C4.+, Relay.pin3, R2.Pin_1
  N4: 3_3V.pin2, 3_3V_2.pin2, VR3.OUT, C5.+, R3.Pin_0, LED3.anode
  N5: D1.cathode, On/Off.pin2
  N6: VR1.IN, VR2.IN, On/Off.pin1, R1.Pin_1, C1.+, C2.+
  N7: LED1.anode, R1.Pin_0
  N8: MC.VCC, JP.pin1
  N9: MC.VIN, JP.pin3
  N10: MC.P0, TSOP.pin4, C6.+, LED3.cathode
  N11: MC.P1, Push_S/W.pin2, R4.Pin_1
  N12: MC.P2, Relay.pin2, LED2.cathode
  N13: MC.P3, ext_pin.pin1
  N14: MC.P4, ext_pin.pin3
  N15: MC.P5, ext_pin.pin2
  N16: R2.Pin_0, LED2.anode
  N17: TSOP.pin2, R3.Pin_1

notes:
  +
  -
  GND
  5V
  CTR
  VCC
  OUT
  SPC-v1.1
  dbagchi
  VIN

custom parts:
  Deb Screw terminal - 2 pins, spacing 0.2in (5.08mm): Screw terminal with 2 pins
  Deb TO-220 Normal Heat Sink: Deb TO-220 Heat Sink (Normal)
  Digispark: The Digispark is an Attiny85 based microcontroller development board similar to the Arduino line, only cheaper, smaller, and a bit less powerful. With a whole host of shields to extend its functionality and the ability to use the familiar Arduino IDE the Digispark is a great way to jump into electronics, or perfect for when an Arduino is too big or too much.
